// Digital circuit t3a1.dig as structural Verilog
module t3a1 (
  input  S0,
  input  S1,
  input  S2,
  output P
);

  wire and_1_out, and_2_out, and_3_out, not_1_out, not_2_out, or_1_out;

  not not_1 (not_1_out, S0);
  not not_2 (not_2_out, S1);
  and and_1 (and_1_out, not_1_out, S1);
  and and_2 (and_2_out, S0, not_2_out);
  and and_3 (and_3_out, S1, S0);
  or or_1 (or_1_out, and_1_out, and_2_out);
  or or_2 (P, or_1_out, and_3_out, S2);
endmodule
