// Digital circuit t1a1.dig as structural Verilog
module t1a1 (
  input  EN0,
  input  J0,
  input  J1,
  input  J2,
  input  J3,
  output S0
);

  wire not_1_out, not_2_out, or_1_out;

  not not_1 (not_1_out, J2);
  not not_2 (not_2_out, J3);
  or or_1 (or_1_out, J0, J1, not_1_out, not_2_out);
  and and_1 (S0, EN0, or_1_out);
endmodule
